// Logisim project cpu.circ as structural Verilog: 2 circuits, main circuit main
module main (
  input  [15:0] INSTRUCTION,
  input  CLOCK,
  output [15:0] FETCH_ADDRESS,
  output Overflow,
  output [15:0] s0_Value,
  output [15:0] s1_Value,
  output [15:0] s2_Value,
  output [15:0] ra_Value,
  output [15:0] sp_Value,
  output [15:0] HI_Value,
  output [15:0] LO_Value
);

  wire MEM_p1, MEM_p3, MEM_p6, MEM_p9, MEM_p12;

  Register #(.width(16)) PC ();  // open: D, en, Q, clk, clr
  Register #(.width(16)) LO ();  // open: D, en, Q, clk, clr
  Register #(.width(16)) HI ();  // open: D, en, Q, clk, clr
  // regfile_main main_1: pin names not known
  // alu_main main_2: pin names not known
  // mem_main MEM: pin names not known; wires that end beside it: MEM_p1, s0_Value, MEM_p3, MEM_p3, s1_Value, MEM_p6, MEM_p6, s2_Value, MEM_p9, MEM_p9, ra_Value, MEM_p12, MEM_p12, sp_Value

  // Other names for the same wires on the sheet: clk = CLOCK; fetch_addr[15:0] = FETCH_ADDRESS

  // Notes on the sheet:
  //   Output
  //   These are outputs/inputs from run.circ
  //   Inputs
  //   These are DEBUG/TEST outputs from your circuit.
endmodule

module Control_signal (
  input  [15:0] Input
);

  wire addi, addiu, andi, branch, jump, lh, lui, memWrite, mfhi, mflo, or_1_out, ori, R, RegWr, sh, slti, U,
       xor_1_out;
  wire [2:0] AluCtr, AluCtr_not_R;

  Multiplexer #(.select(4), .width(3)) multiplexer_1 (
    .in9(3'b011), .in10(3'b100), .out(AluCtr_not_R), .sel(Input[15:12]));  // open: in0, in1, in2, in3, in4, in5, in6, in7, in8, in11, in12, in13, in14, in15, en
  xor xor_1 (xor_1_out, Input[12], Input[13]);
  and isRtype (R, ~Input[12], ~Input[13], ~Input[14], ~Input[15]);  // AND_Gate
  and and_1 (lui, Input[12], ~Input[13], ~Input[14], ~Input[15]);  // AND_Gate
  and and_2 (U, ~xor_1_out, Input[14], Input[15]);  // AND_Gate
  and and_3 (branch, ~Input[15], Input[14], ~Input[13]);  // AND_Gate
  and and_4 (jump, ~Input[15], ~Input[14], Input[13]);  // AND_Gate
  and and_5 (addi, ~Input[15], Input[14], Input[13], ~Input[12]);  // AND_Gate
  and and_6 (addiu, ~Input[15], Input[14], Input[13], Input[12]);  // AND_Gate
  and and_7 (slti, Input[15], ~Input[14], ~Input[13], ~Input[13]);  // AND_Gate
  and and_8 (mfhi, Input[15], Input[14], ~Input[13], Input[12]);  // AND_Gate
  and and_9 (mflo, Input[15], Input[14], Input[13], ~Input[12]);  // AND_Gate
  and and_10 (andi, Input[15], ~Input[14], ~Input[13], Input[12]);  // AND_Gate
  and and_11 (ori, Input[15], ~Input[14], Input[13], ~Input[12]);  // AND_Gate
  and and_12 (lh, Input[15], ~Input[14], Input[13], Input[12]);  // AND_Gate
  and and_13 (sh, Input[15], Input[14], ~Input[13], ~Input[12]);  // AND_Gate
  Multiplexer #(.width(3)) multiplexer_2 (.in0(AluCtr_not_R), .in1(Input[2:0]), .out(AluCtr), .sel(R));  // open: en
  not not_1 (RegWr, or_1_out);
  or or_1 (or_1_out, branch, lui, memWrite);

  // Notes on the sheet:
  //   slti
  //   addi
  //   and
  //   or
  //   addiu
endmodule
